// Logisim project Processor_Tooba_Final.circ as structural Verilog: 9 circuits, main circuit Processor
module Processor (
  input  Reset,
  input  [3:0] Display_Address
);

  wire alu_1_is, alu_1_is_2, branch_unit_1_isbranchtaken, Clock, flags_1_flags_e, flags_1_flags_gt,
       forwarding_unit_3_conflict1, forwarding_unit_3_conflict2, forwarding_unit_4_conflict1,
       forwarding_unit_4_conflict2;
  wire [1:0] forwarding_unit_1_conflict1, forwarding_unit_1_conflict2;
  wire [3:0] multiplexer_7_out, multiplexer_8_out, multiplexer_9_out, register_18_q_2,
       register_file_1_displayd, register_file_1_displayd_2, register_file_1_displayd_4,
       register_file_1_displayd_5, register_file_1_displayd_6, register_file_1_displayd_7,
       register_file_1_displayd_8;
  wire [9:0] control_unit_1_isubranch, register_15_q, register_17_q, register_19_q;
  wire [11:8] register_file_1_displayd_3;
  wire [12:0] control_unit_1_alusignals, register_20_q;
  wire [23:0] PC_q_2;
  wire [26:0] multiplexer_13_out;
  wire [31:0] adder_1_out, adder_2_out, adder_3_out, alu_1_aluresult, bit_extender_1_out,
       calculate_immediate_1_immx, memory_unit_1_ldresult, multiplexer_1_out, multiplexer_2_out,
       multiplexer_3_out, multiplexer_4_out, multiplexer_5_out, multiplexer_6_out, multiplexer_10_out,
       multiplexer_11_out, multiplexer_12_out, multiplexer_14_out, multiplexer_15_out, PC_q, register_1_q,
       register_2_q, register_3_q, register_4_q, register_5_q, register_6_q, register_7_q, register_8_q,
       register_9_q, register_10_q, register_11_q, register_12_q, register_13_q, register_14_q,
       register_16_q, register_18_q, register_file_1_readd1, register_file_1_readd2, rom_1_data,
       shifter_1_out;
  wire [31:27] multiplexer_13_out_2;

  Register #(.width(32), .trigger("falling")) PC (
    .D(multiplexer_2_out), .Q({PC_q[31:26], PC_q_2, PC_q[1:0]}), .clk(Clock), .clr(Reset));  // open: en
  Multiplexer #(.width(32), .enable("false")) multiplexer_1 (
    .in0(register_file_1_readd2), .in1(multiplexer_5_out), .out(multiplexer_1_out),
    .sel(forwarding_unit_3_conflict2));
  Multiplexer #(.width(32), .enable("false")) multiplexer_2 (
    .in0(adder_1_out), .in1(multiplexer_4_out), .out(multiplexer_2_out), .sel(branch_unit_1_isbranchtaken));
  assign bit_extender_1_out = {{5{multiplexer_13_out[26]}}, multiplexer_13_out};  // Bit_Extender bit_extender_1
  Multiplexer #(.width(32), .enable("false")) multiplexer_3 (
    .in0(register_file_1_readd1), .in1(multiplexer_5_out), .out(multiplexer_3_out),
    .sel(forwarding_unit_3_conflict1));
  Adder #(.width(32)) adder_1 (.a(32'h4), .b({PC_q[31:26], PC_q_2, PC_q[1:0]}), .out(adder_1_out));  // open: cin, cout
  Shifter #(.width(32)) shifter_1 (.in(bit_extender_1_out), .\dist (5'b00010), .out(shifter_1_out));
  ALU alu_1 (
    .A(multiplexer_12_out), .B(multiplexer_10_out), .ALUsignals(register_20_q), .aluResult(alu_1_aluresult),
    .is(alu_1_is), .is_2(alu_1_is_2));
  Adder #(.width(32)) adder_2 (.a(register_3_q), .b(32'h4), .out(adder_2_out));  // open: cin, cout
  Calculate_Immediate calculate_immediate_1 (.imm(multiplexer_13_out[17:0]), .immx(calculate_immediate_1_immx));
  Adder #(.width(32)) adder_3 (.a(shifter_1_out), .b(register_4_q), .out(adder_3_out));  // open: cin, cout
  Multiplexer #(.width(32), .enable("false")) multiplexer_4 (
    .in0(register_5_q), .in1(multiplexer_12_out), .out(multiplexer_4_out), .sel(register_15_q[9]));
  Multiplexer #(.select(2), .width(32), .enable("false")) multiplexer_5 (
    .in0(register_11_q), .in1(register_7_q), .in2(adder_2_out), .out(multiplexer_5_out),
    .sel({register_19_q[3], register_19_q[5]}));  // open: in3
  Clock u_Clock (.out(Clock));
  ROM #(.addrWidth(24), .dataWidth(32)) rom_1 (.addr(PC_q_2), .data(rom_1_data));  // open: sel
  Multiplexer #(.width(32), .enable("false")) multiplexer_6 (
    .in0(multiplexer_1_out), .in1(calculate_immediate_1_immx), .out(multiplexer_6_out),
    .sel(control_unit_1_isubranch[7]));
  Flags flags_1 (
    .isCmp(register_20_q[0]), .is(alu_1_is), .is_2(alu_1_is_2), .flags_GT(flags_1_flags_gt),
    .flags_E(flags_1_flags_e));
  Memory_Unit memory_unit_1 (
    .MAR(register_10_q), .ldResult(memory_unit_1_ldresult), .MDR(multiplexer_15_out),
    .isSt(register_17_q[4]), .isLd(register_17_q[5]), .Clock(Clock), .Reset(Reset));
  Hex_Digit_Display hex_digit_display_1 (.value(register_file_1_displayd_8));  // open: dp
  Multiplexer #(.width(4), .enable("false")) multiplexer_7 (
    .in0(multiplexer_13_out[17:14]), .in1(multiplexer_13_out[25:22]), .out(multiplexer_7_out),
    .sel(control_unit_1_isubranch[4]));
  Hex_Digit_Display hex_digit_display_2 (.value(register_file_1_displayd_7));  // open: dp
  Multiplexer #(.width(4), .enable("false")) multiplexer_8 (
    .in0(multiplexer_13_out[21:18]), .in1(4'b1111), .out(multiplexer_8_out), .sel(control_unit_1_isubranch[9]));
  Register_File register_file_1 (
    .ReadA1(multiplexer_8_out), .ReadA2(multiplexer_7_out), .WriteE(register_19_q[8]),
    .WriteD(multiplexer_5_out), .ReadD1(register_file_1_readd1), .ReadD2(register_file_1_readd2),
    .Clock(Clock), .Reset(Reset),
    .DisplayD({register_file_1_displayd_8, register_file_1_displayd_7, register_file_1_displayd_6, register_file_1_displayd_5, register_file_1_displayd_4, register_file_1_displayd_3, register_file_1_displayd_2, register_file_1_displayd}),
    .DisplayA(Display_Address), .WriteA(multiplexer_9_out));
  Hex_Digit_Display hex_digit_display_3 (.value(register_file_1_displayd_6));  // open: dp
  Branch_Unit branch_unit_1 (
    .isBeq(register_15_q[2]), .isUBranch(register_15_q[0]), .flags_E(flags_1_flags_e),
    .isBgt(register_15_q[1]), .flags_GT(flags_1_flags_gt), .isBranchTaken(branch_unit_1_isbranchtaken));
  Hex_Digit_Display hex_digit_display_4 (.value(register_file_1_displayd_5));  // open: dp
  Hex_Digit_Display hex_digit_display_5 (.value(register_file_1_displayd_4));  // open: dp
  Control_Unit control_unit_1 (
    .isSt(control_unit_1_isubranch[4]), .isLd(control_unit_1_isubranch[5]),
    .isBeq(control_unit_1_isubranch[2]), .isBgt(control_unit_1_isubranch[1]),
    .isRet(control_unit_1_isubranch[9]), .I_bit(multiplexer_13_out[26]),
    .isImmediate(control_unit_1_isubranch[7]), .opcode(multiplexer_13_out_2),
    .isWb(control_unit_1_isubranch[8]), .isUbranch(control_unit_1_isubranch[0]),
    .isCall(control_unit_1_isubranch[3]), .ALUsignals(control_unit_1_alusignals));
  Hex_Digit_Display hex_digit_display_6 (.value(register_file_1_displayd_3));  // open: dp
  Hex_Digit_Display hex_digit_display_7 (.value(register_file_1_displayd_2));  // open: dp
  Multiplexer #(.width(4), .enable("false")) multiplexer_9 (
    .in0(register_18_q_2), .in1(4'b1111), .out(multiplexer_9_out), .sel(register_19_q[3]));
  Hex_Digit_Display hex_digit_display_8 (.value(register_file_1_displayd));  // open: dp
  Register #(.width(32)) register_1 (.D(register_4_q), .Q(register_1_q), .clk(Clock));  // open: en, clr
  Register #(.width(32)) register_2 (.D(register_1_q), .Q(register_2_q), .clk(Clock));  // open: en, clr
  Register #(.width(32)) register_3 (.D(register_2_q), .Q(register_3_q), .clk(Clock));  // open: en, clr
  Register #(.width(32)) register_4 (
    .D({PC_q[31:26], PC_q_2, PC_q[1:0]}), .Q(register_4_q), .clk(Clock));  // open: en, clr
  Register #(.width(32)) register_5 (.D(adder_3_out), .Q(register_5_q), .clk(Clock));  // open: en, clr
  Register #(.width(32)) register_6 (.D(multiplexer_6_out), .Q(register_6_q), .clk(Clock));  // open: en, clr
  Multiplexer #(.select(2), .width(32), .enable("false")) multiplexer_10 (
    .in0(register_6_q), .in1(multiplexer_5_out), .in2(register_10_q), .in3(register_10_q),
    .out(multiplexer_10_out), .sel(forwarding_unit_1_conflict2));
  Register #(.width(32)) register_7 (.D(memory_unit_1_ldresult), .Q(register_7_q), .clk(Clock));  // open: en, clr
  Multiplexer #(.width(32), .enable("false")) multiplexer_11 (
    .in0(rom_1_data), .in1(rom_1_data), .out(multiplexer_11_out), .sel(branch_unit_1_isbranchtaken));
  Register #(.width(32)) register_8 (.D(multiplexer_11_out), .Q(register_8_q), .clk(Clock));  // open: en, clr
  Register #(.width(32)) register_9 (.D(multiplexer_3_out), .Q(register_9_q), .clk(Clock));  // open: en, clr
  Multiplexer #(.select(2), .width(32), .enable("false")) multiplexer_12 (
    .in0(register_9_q), .in1(multiplexer_5_out), .in2(register_10_q), .in3(register_10_q),
    .out(multiplexer_12_out), .sel(forwarding_unit_1_conflict1));
  Register #(.width(32)) register_10 (.D(alu_1_aluresult), .Q(register_10_q), .clk(Clock));  // open: en, clr
  Register #(.width(32)) register_11 (.D(register_10_q), .Q(register_11_q), .clk(Clock));  // open: en, clr
  Multiplexer #(.width(32), .enable("false")) multiplexer_13 (
    .in0(register_8_q), .in1(32'h68000000), .out({multiplexer_13_out_2, multiplexer_13_out}),
    .sel(branch_unit_1_isbranchtaken));
  Register #(.width(32)) register_12 (.D(multiplexer_1_out), .Q(register_12_q), .clk(Clock));  // open: en, clr
  Multiplexer #(.width(32), .enable("false")) multiplexer_14 (
    .in0(register_12_q), .in1(multiplexer_5_out), .out(multiplexer_14_out),
    .sel(forwarding_unit_1_conflict2[0]));
  Register #(.width(32)) register_13 (.D(multiplexer_14_out), .Q(register_13_q), .clk(Clock));  // open: en, clr
  Multiplexer #(.width(32), .enable("false")) multiplexer_15 (
    .in0(register_13_q), .in1(multiplexer_5_out), .out(multiplexer_15_out), .sel(forwarding_unit_4_conflict2));
  Register #(.width(32)) register_14 (
    .D({multiplexer_13_out_2, multiplexer_13_out}), .Q(register_14_q), .clk(Clock));  // open: en, clr
  Register #(.width(10)) register_15 (
    .D({control_unit_1_isubranch[9:7], 1'b0, control_unit_1_isubranch[5:0]}), .Q(register_15_q), .clk(Clock));  // open: en, clr
  Register #(.width(32)) register_16 (.D(register_14_q), .Q(register_16_q), .clk(Clock));  // open: en, clr
  Register #(.width(10)) register_17 (.D(register_15_q), .Q(register_17_q), .clk(Clock));  // open: en, clr
  Register #(.width(32)) register_18 (
    .D(register_16_q), .Q({register_18_q[31:26], register_18_q_2, register_18_q[21:0]}), .clk(Clock));  // open: en, clr
  Register #(.width(10)) register_19 (.D(register_17_q), .Q(register_19_q), .clk(Clock));  // open: en, clr
  Register #(.width(13)) register_20 (.D(control_unit_1_alusignals), .Q(register_20_q), .clk(Clock));  // open: en, clr
  Register #(.width(13)) register_21 (.D(register_20_q), .clk(Clock));  // open: en, Q, clr
  Forwarding_Unit forwarding_unit_1 (
    .insA(register_14_q), .insB({register_18_q[31:26], register_18_q_2, register_18_q[21:0]}),
    .conflict2(forwarding_unit_1_conflict2[0]), .conflict1(forwarding_unit_1_conflict1[0]));
  Forwarding_Unit forwarding_unit_2 (
    .insA(register_14_q), .insB(register_16_q), .conflict2(forwarding_unit_1_conflict2[1]),
    .conflict1(forwarding_unit_1_conflict1[1]));
  Forwarding_Unit forwarding_unit_3 (
    .insA({multiplexer_13_out_2, multiplexer_13_out}),
    .insB({register_18_q[31:26], register_18_q_2, register_18_q[21:0]}),
    .conflict2(forwarding_unit_3_conflict2), .conflict1(forwarding_unit_3_conflict1));
  Forwarding_Unit forwarding_unit_4 (
    .insA(register_16_q), .insB({register_18_q[31:26], register_18_q_2, register_18_q[21:0]}),
    .conflict2(forwarding_unit_4_conflict2), .conflict1(forwarding_unit_4_conflict1));

  // Notes on the sheet:
  //   isBranchTaken
  //   ALUsignals
  //   pc
  //   pc+4
  //   branchTarget
  //   offset
  //   pc
  //   B
  //   ALU
  //   aluResult
  //   MAR
  //   calc immx
  //   imm
  //   branchTarget
  //   isBranchTaken
  //   A
  //   is>
  //   is=
  //   MDR
  //   Memory
  //   Unit
  //   ldResult
  //   data
  //   Instruction Memory
  //   contents of rom_1 (hex, n*v repeats v):
  //   4c000173 4c400000 48800000 4d400000 90000007 24c8000a 110cc000 1110c000 1550000 1c88000a 90000001
  //   2c080000 8ffffff9 80000001 28140000 80000002 90000002 4c400001 90000000
  //   immx
  //   isRet
  //   Flags
  //   isCmp
  //   isLd
  //   isSt
  //   isLd
  //   isCall
  //   instruction
  //   rs2
  //   rd
  //   isSt
  //   op2
  //   isImmediate
  //   flags(GT)
  //   flags(E)
  //   rs1
  //   E
  //   Register
  //   A
  //   File
  //   D
  //   op1
  //   Branch
  //   Unit
  //   isRet
  //   isWb
  //   address
  //   data
  //   isBeq
  //   isBgt
  //   isUBranch
  //   Display Register
  //   opcode
  //   CONTROL
  //   I bit
  //   UNIT
  //   5-stage Pipelined Processor with forwarding---Tooba Khan 2021JCS2245
  //   isCall
  //   rd
  //   B Target
  //   PC
  //   PC
  //   PC
  //   B
  //   ldResult
  //   IF/OF Register
  //   A
  //   ALU result
  //   ALU result
  //   Instruction
  //   isUBranch
  //   isBgt
  //   isCall
  //   isSt
  //   OP2
  //   Instr
  //   OP2
  //   Instr
  //   isBeq
  //   isLd
  //   isImmediate
  //   isWb
  //   isRet
  //   Controls
  //   Controls
  //   Controls
  //   ALU signals
  //   ALU signals
  //   conflict in operand 2
  //   conflict in operand 1
  //   conflict in operand 2
  //   conflict in operand 1
  //   conflict in operand 2
  //   conflict in operand 1
  //   conflict in operand 2
  //   conflict in operand 1
  //   RW->EX
  //   MA->EX
  //   RW->OF
  //   RW->MA
endmodule

module Control_Unit (
  input  I_bit,
  input  [4:0] opcode,
  output isSt,
  output isLd,
  output isBeq,
  output isBgt,
  output isRet,
  output isImmediate,
  output isWb,
  output isUbranch,
  output isCall,
  output [12:0] ALUsignals
);

  wire and_6_out, and_7_out, and_8_out, and_9_out, and_10_out, and_12_out, and_13_out, nand_1_out;

  nand nand_1 (nand_1_out, opcode[0], opcode[1]);
  and and_1 (isSt, opcode[0], opcode[1], opcode[2], opcode[3], ~opcode[4]);  // AND_Gate
  and and_2 (isLd, ~opcode[0], opcode[1], opcode[2], opcode[3], ~opcode[4]);  // AND_Gate
  and and_3 (isBeq, ~opcode[0], ~opcode[1], ~opcode[2], ~opcode[3], opcode[4]);  // AND_Gate
  and and_4 (isBgt, opcode[0], ~opcode[1], ~opcode[2], ~opcode[3], opcode[4]);  // AND_Gate
  and and_5 (isRet, ~opcode[0], ~opcode[1], opcode[2], ~opcode[3], opcode[4]);  // AND_Gate
  and and_6 (and_6_out, opcode[0], ~opcode[1], opcode[2], ~opcode[4]);  // AND_Gate
  and and_7 (and_7_out, opcode[0], opcode[2], opcode[3], ~opcode[4]);  // AND_Gate
  and and_8 (and_8_out, opcode[4], nand_1_out);
  and and_9 (and_9_out, opcode[1], ~opcode[2], ~opcode[3], opcode[4]);  // AND_Gate
  and and_10 (and_10_out, ~opcode[0], ~opcode[1], opcode[2], ~opcode[3], opcode[4]);  // AND_Gate
  and and_11 (isCall, opcode[0], opcode[1], ~opcode[2], ~opcode[3], opcode[4]);  // AND_Gate
  and and_12 (and_12_out, ~opcode[0], ~opcode[1], ~opcode[2], ~opcode[3], ~opcode[4]);  // AND_Gate
  and and_13 (and_13_out, opcode[1], opcode[2], opcode[3], ~opcode[4]);  // AND_Gate
  and isSub (ALUsignals[2], opcode[0], ~opcode[1], ~opcode[2], ~opcode[3], ~opcode[4]);  // AND_Gate
  and isCmp (ALUsignals[0], opcode[0], ~opcode[1], opcode[2], ~opcode[3], ~opcode[4]);  // AND_Gate
  and isMul (ALUsignals[3], ~opcode[0], opcode[1], ~opcode[2], ~opcode[3], ~opcode[4]);  // AND_Gate
  and isDiv (ALUsignals[4], opcode[0], opcode[1], ~opcode[2], ~opcode[3], ~opcode[4]);  // AND_Gate
  and isMod (ALUsignals[5], ~opcode[0], ~opcode[1], opcode[2], ~opcode[3], ~opcode[4]);  // AND_Gate
  and isLsl (ALUsignals[7], ~opcode[0], opcode[1], ~opcode[2], opcode[3], ~opcode[4]);  // AND_Gate
  and isLsr (ALUsignals[8], opcode[0], opcode[1], ~opcode[2], opcode[3], ~opcode[4]);  // AND_Gate
  and isAsr (ALUsignals[9], ~opcode[0], ~opcode[1], opcode[2], opcode[3], ~opcode[4]);  // AND_Gate
  and isOr (ALUsignals[12], opcode[0], opcode[1], opcode[2], ~opcode[3], ~opcode[4]);  // AND_Gate
  and isAnd (ALUsignals[11], ~opcode[0], opcode[1], opcode[2], ~opcode[3], ~opcode[4]);  // AND_Gate
  and isNot (ALUsignals[10], ~opcode[0], ~opcode[1], ~opcode[2], opcode[3], ~opcode[4]);  // AND_Gate
  and isMov (ALUsignals[6], opcode[0], ~opcode[1], ~opcode[2], opcode[3], ~opcode[4]);  // AND_Gate
  or or_1 (isUbranch, and_9_out, and_10_out);
  or isAdd (ALUsignals[1], and_12_out, and_13_out);
  nor nor_1 (isWb, and_6_out, and_7_out, and_8_out);

  assign isImmediate = I_bit;

  // Notes on the sheet:
  //   op1
  //   op2
  //   op3
  //   op4
  //   op5
endmodule

module Register_File (
  input  Clock,
  input  Reset,
  input  [31:0] WriteD,
  input  [3:0] ReadA1,
  input  WriteE,
  input  [3:0] WriteA,
  input  [3:0] ReadA2,
  input  [3:0] DisplayA,
  output [31:0] ReadD1,
  output [31:0] ReadD2,
  output [31:0] DisplayD
);

  wire demultiplexer_1_out0, demultiplexer_1_out1, demultiplexer_1_out2, demultiplexer_1_out3,
       demultiplexer_1_out4, demultiplexer_1_out5, demultiplexer_1_out6, demultiplexer_1_out7,
       demultiplexer_1_out8, demultiplexer_1_out9, demultiplexer_1_out10, demultiplexer_1_out11,
       demultiplexer_1_out12, demultiplexer_1_out13, demultiplexer_1_out14, demultiplexer_1_out15,
       multiplexer_2_out, or_1_out, or_2_out;
  wire [31:0] multiplexer_1_out, r0_q, r1_q, r2_q, r3_q, r4_q, r5_q, r6_q, r7_q, r8_q, r9_q, r10_q, r11_q,
       r12_q, r13_q, r14_q, r15_q;

  Demultiplexer #(.select(4), .disabled(0), .enable("false")) demultiplexer_1 (
    .out0(demultiplexer_1_out0), .out1(demultiplexer_1_out1), .out2(demultiplexer_1_out2),
    .out3(demultiplexer_1_out3), .out4(demultiplexer_1_out4), .out5(demultiplexer_1_out5),
    .out6(demultiplexer_1_out6), .out7(demultiplexer_1_out7), .out8(demultiplexer_1_out8),
    .out9(demultiplexer_1_out9), .out10(demultiplexer_1_out10), .out11(demultiplexer_1_out11),
    .out12(demultiplexer_1_out12), .out13(demultiplexer_1_out13), .out14(demultiplexer_1_out14),
    .out15(demultiplexer_1_out15), .in(WriteE), .sel(WriteA));
  Multiplexer #(.width(32), .enable("false")) multiplexer_1 (
    .in0(WriteD), .in1(32'h3fffffc), .out(multiplexer_1_out), .sel(Reset));
  or or_1 (or_1_out, demultiplexer_1_out14, Reset);
  or or_2 (or_2_out, Clock, Reset);
  Multiplexer #(.enable("false")) multiplexer_2 (.in0(or_2_out), .out(multiplexer_2_out), .sel(1'b0));  // open: in1
  Register #(.width(32)) r0 (.D(WriteD), .en(demultiplexer_1_out0), .Q(r0_q), .clk(Clock), .clr(Reset));
  Register #(.width(32)) r1 (.D(WriteD), .en(demultiplexer_1_out1), .Q(r1_q), .clk(Clock), .clr(Reset));
  Register #(.width(32)) r2 (.D(WriteD), .en(demultiplexer_1_out2), .Q(r2_q), .clk(Clock), .clr(Reset));
  Register #(.width(32)) r3 (.D(WriteD), .en(demultiplexer_1_out3), .Q(r3_q), .clk(Clock), .clr(Reset));
  Register #(.width(32)) r4 (.D(WriteD), .en(demultiplexer_1_out4), .Q(r4_q), .clk(Clock), .clr(Reset));
  Register #(.width(32)) r5 (.D(WriteD), .en(demultiplexer_1_out5), .Q(r5_q), .clk(Clock), .clr(Reset));
  Register #(.width(32)) r6 (.D(WriteD), .en(demultiplexer_1_out6), .Q(r6_q), .clk(Clock), .clr(Reset));
  Register #(.width(32)) r7 (.D(WriteD), .en(demultiplexer_1_out7), .Q(r7_q), .clk(Clock), .clr(Reset));
  Register #(.width(32)) r8 (.D(WriteD), .en(demultiplexer_1_out8), .Q(r8_q), .clk(Clock), .clr(Reset));
  Register #(.width(32)) r9 (.D(WriteD), .en(demultiplexer_1_out9), .Q(r9_q), .clk(Clock), .clr(Reset));
  Register #(.width(32)) r10 (.D(WriteD), .en(demultiplexer_1_out10), .Q(r10_q), .clk(Clock), .clr(Reset));
  Register #(.width(32)) r11 (.D(WriteD), .en(demultiplexer_1_out11), .Q(r11_q), .clk(Clock), .clr(Reset));
  Register #(.width(32)) r12 (.D(WriteD), .en(demultiplexer_1_out12), .Q(r12_q), .clk(Clock), .clr(Reset));
  Register #(.width(32)) r13 (.D(WriteD), .en(demultiplexer_1_out13), .Q(r13_q), .clk(Clock), .clr(Reset));
  Register #(.width(32)) r14 (.D(multiplexer_1_out), .en(or_1_out), .Q(r14_q), .clk(multiplexer_2_out));  // open: clr
  Register #(.width(32)) r15 (.D(WriteD), .en(demultiplexer_1_out15), .Q(r15_q), .clk(Clock), .clr(Reset));
  Multiplexer #(.select(4), .width(32), .disabled(0), .enable("false")) multiplexer_3 (
    .in0(r0_q), .in1(r1_q), .in2(r2_q), .in3(r3_q), .in4(r4_q), .in5(r5_q), .in6(r6_q), .in7(r7_q),
    .in8(r8_q), .in9(r9_q), .in10(r10_q), .in11(r11_q), .in12(r12_q), .in13(r13_q), .in14(r14_q),
    .in15(r15_q), .out(ReadD1), .sel(ReadA1));
  Multiplexer #(.select(4), .width(32), .disabled(0), .enable("false")) multiplexer_4 (
    .in0(r0_q), .in1(r1_q), .in2(r2_q), .in3(r3_q), .in4(r4_q), .in5(r5_q), .in6(r6_q), .in7(r7_q),
    .in8(r8_q), .in9(r9_q), .in10(r10_q), .in11(r11_q), .in12(r12_q), .in13(r13_q), .in14(r14_q),
    .in15(r15_q), .out(ReadD2), .sel(ReadA2));
  Multiplexer #(.select(4), .width(32), .disabled(0), .enable("false")) multiplexer_5 (
    .in0(r0_q), .in1(r1_q), .in2(r2_q), .in3(r3_q), .in4(r4_q), .in5(r5_q), .in6(r6_q), .in7(r7_q),
    .in8(r8_q), .in9(r9_q), .in10(r10_q), .in11(r11_q), .in12(r12_q), .in13(r13_q), .in14(r14_q),
    .in15(r15_q), .out(DisplayD), .sel(DisplayA));
endmodule

module ALU (
  input  [31:0] A,
  input  [31:0] B,
  input  [12:0] ALUsignals,
  output [31:0] aluResult,
  output is,
  output is_2
);

  wire [31:0] adder_1_out, and_1_out, divider_1_out, divider_1_rem, multiplier_1_out, not_1_out, or_1_out,
       shifter_1_out, shifter_2_out, shifter_3_out, subtractor_1_out;

  Adder #(.width(32)) adder_1 (.a(A), .b(B), .out(adder_1_out));  // open: cin, cout
  Subtractor #(.width(32)) subtractor_1 (.a(A), .b(B), .out(subtractor_1_out));  // open: bin, bout
  Multiplier #(.width(32)) multiplier_1 (.a(A), .b(B), .out(multiplier_1_out));  // open: cin, cout
  Divider #(.width(32)) divider_1 (.a(A), .b(B), .out(divider_1_out), .rem(divider_1_rem));  // open: upper
  Comparator #(.width(32)) comparator_1 (.a(A), .b(B), .gt(is), .eq(is_2));  // open: lt
  Shifter #(.width(32)) shifter_1 (.in(A), .\dist (B[4:0]), .out(shifter_1_out));
  Shifter #(.width(32), .shift("lr")) shifter_2 (.in(A), .\dist (B[4:0]), .out(shifter_2_out));
  Shifter #(.width(32), .shift("ar")) shifter_3 (.in(A), .\dist (B[4:0]), .out(shifter_3_out));
  assign not_1_out = ~B;  // NOT_Gate not_1, 32 bits wide
  assign and_1_out = A & B;  // AND_Gate and_1, 32 bits wide
  assign or_1_out = A | B;  // OR_Gate or_1, 32 bits wide
  assign aluResult = ALUsignals[1] ? adder_1_out : 32'bz;  // Controlled_Buffer controlled_buffer_1
  assign aluResult = ALUsignals[2] ? subtractor_1_out : 32'bz;  // Controlled_Buffer controlled_buffer_2
  assign aluResult = ALUsignals[3] ? multiplier_1_out : 32'bz;  // Controlled_Buffer controlled_buffer_3
  assign aluResult = ALUsignals[4] ? divider_1_out : 32'bz;  // Controlled_Buffer controlled_buffer_4
  assign aluResult = ALUsignals[5] ? divider_1_rem : 32'bz;  // Controlled_Buffer controlled_buffer_5
  assign aluResult = ALUsignals[6] ? B : 32'bz;  // Controlled_Buffer controlled_buffer_6
  assign aluResult = ALUsignals[7] ? shifter_1_out : 32'bz;  // Controlled_Buffer controlled_buffer_7
  assign aluResult = ALUsignals[8] ? shifter_2_out : 32'bz;  // Controlled_Buffer controlled_buffer_8
  assign aluResult = ALUsignals[9] ? shifter_3_out : 32'bz;  // Controlled_Buffer controlled_buffer_9
  assign aluResult = ALUsignals[10] ? not_1_out : 32'bz;  // Controlled_Buffer controlled_buffer_10
  assign aluResult = ALUsignals[11] ? and_1_out : 32'bz;  // Controlled_Buffer controlled_buffer_11
  assign aluResult = ALUsignals[12] ? or_1_out : 32'bz;  // Controlled_Buffer controlled_buffer_12

  // Notes on the sheet:
  //   add
  //   sub
  //   mul
  //   div
  //   cmp
  //   lsr
  //   mod
  //   lsl
  //   asr
endmodule

module Flags (
  input  isCmp,
  input  is,
  input  is_2,
  output flags_GT,
  output flags_E
);

  D_Flip_Flop #(.trigger("high")) d_ff_1 (.clk(isCmp), .D(is), .Q(flags_GT));  // open: Qn, preset, en, reset
  D_Flip_Flop #(.trigger("high")) d_ff_2 (.clk(isCmp), .D(is_2), .Q(flags_E));  // open: Qn, preset, en, reset
endmodule

module Branch_Unit (
  input  isUBranch,
  input  isBeq,
  input  flags_E,
  input  isBgt,
  input  flags_GT,
  output isBranchTaken
);

  wire and_1_out, and_2_out;

  and and_1 (and_1_out, isBeq, flags_E);
  and and_2 (and_2_out, isBgt, flags_GT);
  or or_1 (isBranchTaken, isUBranch, and_1_out, and_2_out);
endmodule

module Memory_Unit (
  input  [31:0] MAR,
  input  isLd,
  input  [31:0] MDR,
  input  isSt,
  input  Clock,
  input  Reset,
  output [31:0] ldResult
);

  RAM #(.addrWidth(24), .dataWidth(32), .bus("separate")) ram_1 (
    .addr(MAR[25:2]), .din(MDR), .data(ldResult), .str(isSt), .clk(Clock), .ld(isLd), .clr(Reset));  // open: sel
endmodule

module Calculate_Immediate (
  input  [17:0] imm,
  output [31:0] immx
);

  wire [31:0] bit_extender_1_out, bit_extender_2_out, shifter_1_out;

  assign bit_extender_1_out = {{16{1'b0}}, imm[15:0]};  // Bit_Extender bit_extender_1
  assign bit_extender_2_out = {{16{imm[15]}}, imm[15:0]};  // Bit_Extender bit_extender_2
  Shifter #(.width(32)) shifter_1 (.in(bit_extender_1_out), .\dist (5'b10000), .out(shifter_1_out));
  Multiplexer #(.select(2), .width(32), .enable("false")) multiplexer_1 (
    .in0(bit_extender_2_out), .in1(bit_extender_1_out), .in2(shifter_1_out), .out(immx), .sel(imm[17:16]));  // open: in3

  // Notes on the sheet:
  //   modifier bits
  //   high
  //   default
  //   unsigned
endmodule

module Forwarding_Unit (
  input  [31:0] insA,
  input  [31:0] insB,
  output conflict2,
  output conflict1
);

  wire and_2_out, comparator_1_eq, comparator_2_eq, comparator_3_eq, comparator_4_eq, comparator_5_eq,
       comparator_6_eq, comparator_7_eq, comparator_8_eq, comparator_9_eq, comparator_10_eq,
       comparator_11_eq, comparator_12_eq, comparator_13_eq, comparator_14_eq, comparator_15_eq,
       comparator_16_eq, comparator_17_eq, comparator_18_eq, comparator_19_eq, comparator_20_eq,
       comparator_21_eq, comparator_22_eq, comparator_23_eq, comparator_24_eq, comparator_25_eq,
       comparator_26_eq, comparator_27_eq, comparator_28_eq, comparator_29_eq, comparator_30_eq,
       comparator_31_eq, comparator_32_eq, comparator_33_eq, comparator_34_eq, comparator_35_eq,
       multiplexer_3_out, multiplexer_6_out, not_1_out, not_2_out, not_3_out, not_4_out, or_1_out, or_2_out,
       or_3_out, or_4_out, or_5_out, or_6_out, or_7_out, or_8_out;
  wire [3:0] multiplexer_1_out, multiplexer_2_out, multiplexer_4_out, multiplexer_5_out;

  Comparator #(.width(5)) comparator_1 (.a(insA[31:27]), .b(5'b01000), .eq(comparator_1_eq));  // open: gt, lt
  Comparator #(.width(5)) comparator_2 (.a(insA[31:27]), .b(5'b01001), .eq(comparator_2_eq));  // open: gt, lt
  Comparator #(.width(5)) comparator_3 (.a(insA[31:27]), .b(5'b01101), .eq(comparator_3_eq));  // open: gt, lt
  Comparator #(.width(5)) comparator_4 (.a(insA[31:27]), .b(5'b10000), .eq(comparator_4_eq));  // open: gt, lt
  Comparator #(.width(5)) comparator_5 (.a(insA[31:27]), .b(5'b10001), .eq(comparator_5_eq));  // open: gt, lt
  Comparator #(.width(5)) comparator_6 (.a(insA[31:27]), .b(5'b10010), .eq(comparator_6_eq));  // open: gt, lt
  Comparator #(.width(5)) comparator_7 (.a(insA[31:27]), .b(5'b10011), .eq(comparator_7_eq));  // open: gt, lt
  Comparator #(.width(5)) comparator_8 (.a(insB[31:27]), .b(5'b01111), .eq(comparator_8_eq));  // open: gt, lt
  Comparator #(.width(5)) comparator_9 (.a(insB[31:27]), .b(5'b00101), .eq(comparator_9_eq));  // open: gt, lt
  Comparator #(.width(5)) comparator_10 (.a(insB[31:27]), .b(5'b01101), .eq(comparator_10_eq));  // open: gt, lt
  Comparator #(.width(5)) comparator_11 (.a(insB[31:27]), .b(5'b10100), .eq(comparator_11_eq));  // open: gt, lt
  Comparator #(.width(5)) comparator_12 (.a(insB[31:27]), .b(5'b10001), .eq(comparator_12_eq));  // open: gt, lt
  Comparator #(.width(5)) comparator_13 (.a(insB[31:27]), .b(5'b10010), .eq(comparator_13_eq));  // open: gt, lt
  Comparator #(.width(5)) comparator_14 (.a(insB[31:27]), .b(5'b10011), .eq(comparator_14_eq));  // open: gt, lt
  or or_1 (or_1_out, comparator_1_eq, comparator_2_eq, comparator_3_eq, comparator_4_eq, comparator_5_eq, comparator_6_eq, comparator_7_eq);
  or or_2 (or_2_out, comparator_8_eq, comparator_9_eq, comparator_10_eq, comparator_11_eq, comparator_12_eq, comparator_13_eq, comparator_14_eq);
  or or_3 (or_3_out, or_1_out, or_2_out);
  Comparator #(.width(5)) comparator_15 (.a(insA[31:27]), .b(5'b10100), .eq(comparator_15_eq));  // open: gt, lt
  Comparator #(.width(5)) comparator_16 (.a(insB[31:27]), .b(5'b10011), .eq(comparator_16_eq));  // open: gt, lt
  Multiplexer #(.width(4)) multiplexer_1 (
    .in0(insA[21:18]), .in1(4'b1111), .out(multiplexer_1_out), .sel(comparator_15_eq), .en(not_1_out));
  Multiplexer #(.width(4)) multiplexer_2 (
    .in0(insB[25:22]), .in1(4'b1111), .out(multiplexer_2_out), .sel(comparator_16_eq), .en(not_1_out));
  not not_1 (not_1_out, or_3_out);
  Comparator #(.width(4)) comparator_17 (
    .a(multiplexer_1_out), .b(multiplexer_2_out), .eq(comparator_17_eq));  // open: gt, lt
  Comparator #(.width(32)) comparator_18 (.a({32{1'b0}}), .b(insA), .eq(comparator_18_eq));  // open: gt, lt
  Comparator #(.width(32)) comparator_19 (.a({32{1'b0}}), .b(insB), .eq(comparator_19_eq));  // open: gt, lt
  or or_4 (or_4_out, comparator_18_eq, comparator_19_eq);
  Multiplexer multiplexer_3 (.in0(comparator_17_eq), .in1(1'b0), .out(multiplexer_3_out), .sel(or_3_out));  // open: en
  and and_1 (conflict1, multiplexer_3_out, not_2_out);
  not not_2 (not_2_out, or_4_out);
  Comparator #(.width(5)) comparator_20 (.a(insA[31:27]), .b(5'b01111), .eq(comparator_20_eq));  // open: gt, lt
  Comparator #(.width(5)) comparator_21 (.a(insA[31:27]), .b(5'b01101), .eq(comparator_21_eq));  // open: gt, lt
  Comparator #(.width(5)) comparator_22 (.a(insA[31:27]), .b(5'b10000), .eq(comparator_22_eq));  // open: gt, lt
  Comparator #(.width(5)) comparator_23 (.a(insA[31:27]), .b(5'b10001), .eq(comparator_23_eq));  // open: gt, lt
  Comparator #(.width(5)) comparator_24 (.a(insA[31:27]), .b(5'b10010), .eq(comparator_24_eq));  // open: gt, lt
  Comparator #(.width(5)) comparator_25 (.a(insA[31:27]), .b(5'b10011), .eq(comparator_25_eq));  // open: gt, lt
  not not_3 (not_3_out, comparator_20_eq);
  Comparator #(.width(5)) comparator_26 (.a(insB[31:27]), .b(5'b01111), .eq(comparator_26_eq));  // open: gt, lt
  Comparator #(.width(5)) comparator_27 (.a(insB[31:27]), .b(5'b00101), .eq(comparator_27_eq));  // open: gt, lt
  Comparator #(.width(5)) comparator_28 (.a(insB[31:27]), .b(5'b01101), .eq(comparator_28_eq));  // open: gt, lt
  Comparator #(.width(5)) comparator_29 (.a(insB[31:27]), .b(5'b10000), .eq(comparator_29_eq));  // open: gt, lt
  Comparator #(.width(5)) comparator_30 (.a(insB[31:27]), .b(5'b10001), .eq(comparator_30_eq));  // open: gt, lt
  Comparator #(.width(5)) comparator_31 (.a(insB[31:27]), .b(5'b10010), .eq(comparator_31_eq));  // open: gt, lt
  Comparator #(.width(5)) comparator_32 (.a(insB[31:27]), .b(5'b10011), .eq(comparator_32_eq));  // open: gt, lt
  and and_2 (and_2_out, not_3_out, insA[26]);
  or or_5 (or_5_out, comparator_21_eq, comparator_22_eq, comparator_23_eq, comparator_24_eq, comparator_25_eq);
  or or_6 (or_6_out, comparator_26_eq, comparator_27_eq, comparator_28_eq, comparator_29_eq, comparator_30_eq, comparator_31_eq, comparator_32_eq);
  or or_7 (or_7_out, or_5_out, or_6_out);
  Comparator #(.width(5)) comparator_33 (.a(insA[31:27]), .b(5'b01111), .eq(comparator_33_eq));  // open: gt, lt
  Comparator #(.width(5)) comparator_34 (.a(insB[31:27]), .b(5'b10011), .eq(comparator_34_eq));  // open: gt, lt
  or or_8 (or_8_out, and_2_out, or_7_out);
  Multiplexer #(.width(4)) multiplexer_4 (
    .in0(insA[17:14]), .in1(insA[25:22]), .out(multiplexer_4_out), .sel(comparator_33_eq), .en(not_4_out));
  Multiplexer #(.width(4)) multiplexer_5 (
    .in0(insB[25:22]), .in1(4'b1111), .out(multiplexer_5_out), .sel(comparator_34_eq), .en(not_4_out));
  not not_4 (not_4_out, or_7_out);
  Comparator #(.width(4)) comparator_35 (
    .a(multiplexer_4_out), .b(multiplexer_5_out), .eq(comparator_35_eq));  // open: gt, lt
  Multiplexer multiplexer_6 (.in0(comparator_35_eq), .in1(1'b0), .out(multiplexer_6_out), .sel(or_8_out));  // open: en
  and and_3 (conflict2, not_2_out, multiplexer_6_out);

  // Notes on the sheet:
  //   A.opcode i.e instruction from OF stage
  //   B.opcode i.e instruction from RW stage
  //   A.rs1
  //   ra
  //   A.opcode
  //   B.rd
  //   ra
  //   B.opcode
  //   src 1
  //   If A is a return instruction
  //   If B is a call instruction
  //   if forwarding is not needed this will result to 0
  //   dest
  //   ra
  //   Comparison for operand 1
  //   A.I
  //   A.opcode i.e instruction from OF stage
  //   B.opcode i.e instruction from RW stage
  //   If A.opcode != st
  //   A.rs2
  //   A.rd
  //   A.opcode
  //   B.rd
  //   ra
  //   B.opcode
  //   if forwarding is not needed this will result to 0
  //   src 2
  //   If A is a store instruction
  //   dest
  //   If B is a call instruction
  //   Comparison for operand 2
endmodule
